# Fritzing sketch WiFi RGB LED Strip (saved by Fritzing 0.9.2b)
breadboards: 1

parts:
  Q1 = Basic FET P-Channel [package="TO220 [THT]"]
  Q2 = Basic FET P-Channel [package="TO220 [THT]"]
  Q3 = Basic FET P-Channel [package="TO220 [THT]"]
  Bauteil1 = Arduino Nano (Rev3.0)
  R2 = Resistor [tolerance=±5% resistance=220 package=THT]
  R3 = Resistor [tolerance=±5% resistance=220 package=THT]
  R4 = Resistor [tolerance=±5% resistance=220 package=THT]
  LED1 = RGB LED (com. cathode, rgb) [package="5 mm [THT]"]
  U1 = ESP8266 WiFi Module [part_number=ESP8266]
  IC1 = Voltage Regulator [package=78xxl]
  R5 = Resistor [tolerance=±5% resistance=2k package=THT]
  R6 = Resistor [tolerance=±5% resistance=1k package=THT]
  IC2 = V_REG_LD1117VXX [package=78xxl]

nets:
  N1: Q1.gate, R4.Pin_1
  N2: Q1.drain, LED1.green_anode
  GND: Q1.source, Q2.source, Q3.source, Bauteil1.GND, U1.GND, IC1.GND, R5.Pin_0, IC2.GND
  N3: Q2.gate, R2.Pin_1
  N4: Q2.drain, LED1.blue_anode
  N5: Q3.gate, R3.Pin_1
  N6: Q3.drain, LED1.red_anode
  N7: Bauteil1.D3, R4.Pin_0
  N8: Bauteil1.D5, R2.Pin_0
  N9: Bauteil1.D6, R3.Pin_0
  N10: Bauteil1.D10, U1.TXD
  N11: Bauteil1.D11/MOSI, R5.Pin_1, R6.Pin_0
  12V: Bauteil1.VIN, LED1.common_cathode, IC1.IN
  N12: U1.RXD, R6.Pin_1
  N13: U1.VCC, U1.CH_PD, IC2.OUT
  N14: IC1.OUT, IC2.IN

custom parts:
  ESP8266 WiFi Module: Generic WiFi Module based on the ESP8266 with onboard PCB antenna and UART communications
